// Digital circuit DECODER.dig as structural Verilog
module DECODER (
  input  [3:0] OPCODE,
  input  ZERO,
  input  CARRY,
  output [2:0] ALU_SEL,
  output REG_WE,
  output RAM_CS,
  output RAM_WE,
  output RAM_OE,
  output PC_EN,
  output JUMP_EN,
  output HALT
);

  wire decoder_1_out_3, decoder_1_out_4, decoder_1_out_5, decoder_1_out_6, decoder_1_out_7, decoder_1_out_8,
       decoder_1_out_9, decoder_1_out_10, decoder_1_out_11, decoder_1_out_13, decoder_1_out_14;

  Decoder #(.Selector_Bits(4)) decoder_1 (
    .sel(OPCODE), .out_1(RAM_OE), .out_2(RAM_WE), .out_3(decoder_1_out_3), .out_4(decoder_1_out_4),
    .out_5(decoder_1_out_5), .out_6(decoder_1_out_6), .out_7(decoder_1_out_7), .out_8(decoder_1_out_8),
    .out_9(decoder_1_out_9), .out_10(decoder_1_out_10), .out_11(decoder_1_out_11), .out_13(decoder_1_out_13),
    .out_14(decoder_1_out_14), .out_15(HALT));  // open: out_0, out_12
  not not_1 (PC_EN, HALT);
  or or_1 (REG_WE, RAM_OE, decoder_1_out_3, decoder_1_out_4, decoder_1_out_5, decoder_1_out_6, decoder_1_out_7, decoder_1_out_8, decoder_1_out_9, decoder_1_out_10, decoder_1_out_11);
  or or_2 (RAM_CS, RAM_OE, RAM_WE);
  and and_1 (decoder_1_out_8, decoder_1_out_14, ZERO);
  or or_3 (ALU_SEL[2], decoder_1_out_8, decoder_1_out_9, decoder_1_out_10, decoder_1_out_11);
  or or_4 (JUMP_EN, decoder_1_out_13, decoder_1_out_8);
  or or_5 (ALU_SEL[0], decoder_1_out_5, decoder_1_out_9, decoder_1_out_10, decoder_1_out_11);
  or or_6 (ALU_SEL[1], decoder_1_out_6, decoder_1_out_7, decoder_1_out_10, decoder_1_out_11);

  // Notes on the sheet:
  //   OPCODE: From IR
  //   ZERO: From ALU
  //   CARRY: From ALU
endmodule
