// Digital circuit ROM.dig as structural Verilog
module ROM (
  input  [7:0] ADDRESS,
  output [15:0] INSTRUCTION
);

  ROM #(.AddrBits(8), .Bits(16)) ROM (.A(ADDRESS), .sel(1'b1), .D(INSTRUCTION));
endmodule
